# Fritzing sketch digispark_low_voltage_disconnect (saved by Fritzing 0.9.3b)
breadboards: 1

parts:
  R9 = Resistor [tolerance=±5% resistance=100 package="0805 [SMD]"]
  power_from_5V_DC_boost = Power plug
  Digispark1 = Digispark
  R18 = Resistor [tolerance=±5% resistance=1k package="2010 [SMD]"]
  Q2 = Basic FET N-Channel [package="D2Pak [SMD]"]
  5V_with_low_voltage_disconnect = Power plug

nets:
  N1: R9.Pin_0, Digispark1.P1
  N2: R9.Pin_1, Q2.Gate
  GND: power_from_5V_DC_boost.GND, Digispark1.GND, R18.Pin_0, Q2.drain
  VCC: power_from_5V_DC_boost.VCC, Digispark1.VIN, 5V_with_low_voltage_disconnect.VCC
  N3: Digispark1.P0, R18.Pin_1
  N4: Q2.source, 5V_with_low_voltage_disconnect.GND

notes:
  connect to batteries (+)

custom parts:
  Digispark: The Digispark is an Attiny85 based microcontroller development board similar to the Arduino line, only cheaper, smaller, and a bit less powerful. With a whole host of shields to extend its functionality and the ability to use the familiar Arduino IDE the Digispark is a great way to jump into electronics, or perfect for when an Arduino is too big or too much.
