# Fritzing sketch gamepad_with_3_buttons (saved by Fritzing 0.9.3b)
breadboards: 1

parts:
  S2 = Round Pushbutton
  R2 = Resistor [tolerance=±5% resistance=47 package="0805 [SMD]"]
  Bauteil1 = ESP32 Module Testbed  # not connected
  S4 = Round Pushbutton
  R3 = Resistor [tolerance=±5% resistance=22k package="0805 [SMD]"]
  R4 = Resistor [tolerance=±5% resistance=22k package="0805 [SMD]"]
  LED3 = RGB LED (com. cathode, rbg) [package="5 mm [THT]"]
  LED4 = RGB LED (com. cathode, rbg) [package="5 mm [THT]"]
  R5 = Resistor [tolerance=±5% resistance=47 package="0805 [SMD]"]
  R6 = Resistor [tolerance=±5% resistance=22k package="0805 [SMD]"]
  S5 = Round Pushbutton
  LED5 = RGB LED (com. cathode, rbg) [package="5 mm [THT]"]
  R7 = Resistor [tolerance=±5% resistance=47 package="0805 [SMD]"]
  R8 = Resistor [tolerance=±5% resistance=47 package="0805 [SMD]"]
  R9 = Resistor [tolerance=±5% resistance=10 package="0805 [SMD]"]
  R10 = Resistor [tolerance=±5% resistance=10 package="0805 [SMD]"]
  R11 = Resistor [tolerance=±5% resistance=47 package="0805 [SMD]"]
  R12 = Resistor [tolerance=±5% resistance=47 package="0805 [SMD]"]
  R13 = Resistor [tolerance=±5% resistance=10 package="0805 [SMD]"]
  5V_power_supply = Power plug

nets:
  N1: S2.leg0, S4.leg0, LED3.common_cathode, LED4.common_cathode, S5.leg0, 5V_power_supply.GND
  N2: S2.leg1, R4.Pin_0
  N3: R2.Pin_0, LED3.red_anode
  N4: S4.leg1, R3.Pin_0
  N5: R3.Pin_1, R4.Pin_1, R6.Pin_1, 5V_power_supply.VCC
  N6: LED3.blue_anode, R9.Pin_0
  N7: LED3.green_anode, R8.Pin_0
  N8: LED4.red_anode, R11.Pin_0
  N9: LED4.blue_anode, R10.Pin_0
  N10: LED4.green_anode, R5.Pin_0
  N11: R6.Pin_0, S5.leg1
  N12: LED5.red_anode, R7.Pin_0
  N13: LED5.blue_anode, R13.Pin_0
  N14: LED5.green_anode, R12.Pin_0

notes:
  Attention, PINs are slightly different on the used ESP32 dev module!
  connect to batteries (+)
  to detect low voltage
  Battery Management System (for charging)
  2 Li-Ion Batteries in parallel (4.2V - 3.4V)
  230v AC Powerplug
  to 5V DC
  5V Step Up Module

custom parts:
  ESP32 Module Testbed: The ESP32 Module Testbed is a breadboard compatible breakout board for the ESP-WROOM-03 ESP32 module. The ESP32 is a WiFi and Bluetooth-enabled 32-bit, dual-core microcontroller.
