# Fritzing sketch low_voltage_batteries_protection (saved by Fritzing 0.9.3b)
breadboards: 1

parts:
  R6 = Resistor [tolerance=±5% resistance=100 package="0805 [SMD]"]
  5V_power_supply = Power plug
  U1 = attiny85 [package=dip]
  Q1 = Basic FET N-Channel [package="TO220 [THT]"]
  R15 = Resistor [tolerance=±5% resistance=100 package="0805 [SMD]"]
  LED6 = smd LED [color="Red (633nm)" package="0805 [SMD]"]
  R3 = Resistor [tolerance=±5% resistance=10k package="0805 [SMD]"]

nets:
  N1: R6.Pin_0, Q1.gate, R3.Pin_1
  N2: R6.Pin_1, U1.Pin_1
  N3: 5V_power_supply.GND, U1.Pin_4, Q1.source, R3.Pin_0
  N4: 5V_power_supply.VCC, U1.Pin_8
  N5: U1.Pin_2, R15.Pin_1
  N6: R15.Pin_0, LED6.anode

notes:
  yellow cable to batteries
  5V power output if batteries are > 3V
  (low side switching)
